// Logisim project 24bit.circ as structural Verilog: 7 circuits, main circuit main
module main (
  input  ENABLE,
  input  MANUAL,
  input  TURN_ON,
  input  EnableClock,
  input  UNLOCK,
  input  TurnOnMonitor
);

  wire add, alu_1_borrow, alu_1_carry, alu_1_equal, alu_1_greater, alu_1_less, alu_1_zero, and1, and_1_out,
       and_2_out, and_3_out, BORROW, CARRY, CLEAR_out, clock_1_out, cock, comparator_1_eq, div, draw, E, G,
       gpr_r, gpr_w, GPU_WRITE, halt, JE, JnotE, jump, keybrd, L, load, manual_t, mult, not1, not_1_out,
       not_2_out, not_3_out, not_4_out, or1, or_1_out, or_2_out, or_3_out, pull_resistor_2_node, ram_r,
       ram_w, RESET, sub, text, xor1, ZERO;
  wire [1:0] cmd;
  wire [3:0] A, B, C, D, multiplexer_3_out;
  wire [5:0] gpu_1_x_out, gpu_1_y_out;
  wire [6:0] controlled_buffer_4_out, keyboard_1_data, pull_resistor_3_node;
  wire [7:0] COLOR_sw8, gpu_1_color_out, ram_1_dout;
  wire [21:19] rom_1_data;
  wire [23:0] bit_extender_1_out, cntr, gpr_1_l0, gpr_1_l1, gpr_1_l2, gpr_1_l3, gpr_1_l4, gpr_1_l5, gpr_1_l6,
       gpr_1_l7, gpr_1_l8, gpr_1_l9, gpr_1_l10, gpr_1_l11, gpr_1_l12, gpr_1_l13, gpr_1_l14, gpr_1_l15,
       multiplexer_2_out, ram_2_dout, XY;
  wire [23:7] pull_resistor_3_node_2;

  RAM #(.addrWidth(12), .dataWidth(24)) ram_1 (
    .addr(cntr[11:0]), .oe(TURN_ON), .clk(cock), .dout({D, C, B, A, ram_1_dout}));  // open: we, din
  Pull_Resistor pull_resistor_1 (.node({D, C, B, A, ram_1_dout}));
  Hex_Digit_Display hex_digit_display_1 (.value(A));  // open: dp
  Hex_Digit_Display hex_digit_display_2 (.value(B));  // open: dp
  Hex_Digit_Display hex_digit_display_3 (.value(C));  // open: dp
  Hex_Digit_Display hex_digit_display_4 (.value(D));  // open: dp
  ROM #(.dataWidth(24)) rom_1 (
    .addr(ram_1_dout),
    .data({cmd, rom_1_data, load, keybrd, text, JnotE, JE, not1, xor1, or1, and1, div, mult, sub, add, ram_r, gpr_r, ram_w, gpr_w, jump, halt}));
  or or_1 (or_1_out, ENABLE, EnableClock);
  or or_2 (or_2_out, MANUAL, manual_t);
  not not_1 (not_1_out, comparator_1_eq);
  Comparator #(.width(24)) comparator_1 (.a({24{1'b0}}), .b(cntr), .eq(comparator_1_eq));  // open: gt, lt
  Clock clock_1 (.out(clock_1_out));
  CLK clk_1 (.CLOCK(clock_1_out), .ENABLE(or_1_out), .MANUAL(or_2_out), .HALT(pull_resistor_2_node), .CLOCKOUT(cock));
  Pull_Resistor pull_resistor_2 (.node(pull_resistor_2_node));
  assign pull_resistor_2_node = UNLOCK ? and_1_out : 1'bz;  // Controlled_Buffer controlled_buffer_1
  and and_1 (and_1_out, halt, not_1_out);
  LED led_1 (.in(pull_resistor_3_node_2[23]));
  LED led_2 (.in(pull_resistor_3_node_2[22]));
  assign bit_extender_1_out = {{12{1'b0}}, {D, C, B}};  // Bit_Extender bit_extender_1
  LED led_3 (.in(pull_resistor_3_node_2[21]));
  LED led_4 (.in(pull_resistor_3_node_2[20]));
  LED led_5 (.in(pull_resistor_3_node_2[19]));
  LED led_6 (.in(pull_resistor_3_node_2[18]));
  Pull_Resistor pull_resistor_3 (.node({pull_resistor_3_node_2, pull_resistor_3_node}));
  assign {pull_resistor_3_node_2, pull_resistor_3_node} = load ? bit_extender_1_out : 24'bz;  // Controlled_Buffer controlled_buffer_2
  LED led_7 (.in(pull_resistor_3_node_2[17]));
  LED led_8 (.in(pull_resistor_3_node_2[16]));
  LED led_9 (.in(pull_resistor_3_node_2[15]));
  LED led_10 (.in(pull_resistor_3_node_2[14]));
  not not_2 (not_2_out, draw);
  D_Flip_Flop d_ff_1 (.clk(rom_1_data[19]), .D(not_2_out), .Q(draw));  // open: Qn, preset, reset
  not not_3 (not_3_out, GPU_WRITE);
  D_Flip_Flop d_ff_2 (.clk(rom_1_data[20]), .D(not_3_out), .Q(GPU_WRITE));  // open: Qn, preset, reset
  LED led_11 (.in(pull_resistor_3_node_2[13]));
  LED led_12 (.in(pull_resistor_3_node_2[12]));
  LED led_13 (.in(pull_resistor_3_node_2[11]));
  LED led_14 (.in(pull_resistor_3_node_2[10]));
  assign {pull_resistor_3_node_2, pull_resistor_3_node} = {{17{1'b0}}, controlled_buffer_4_out};  // Bit_Extender bit_extender_2
  LED led_15 (.in(cntr[23]));
  LED led_16 (.in(cntr[22]));
  LED led_17 (.in(cntr[21]));
  LED led_18 (.in(cntr[20]));
  LED led_19 (.in(pull_resistor_3_node_2[9]));
  LED led_20 (.in(pull_resistor_3_node_2[8]));
  LED led_21 (.in(pull_resistor_3_node_2[7]));
  LED led_22 (.in(pull_resistor_3_node[6]));
  GPU gpu_1 (
    .XY(XY[11:0]), .WRITE(GPU_WRITE), .RESET(RESET), .DRAW(draw), .CLOCK(cock), .COLOR(COLOR_sw8),
    .ENABLE(TURN_ON), .COLOR_OUT(gpu_1_color_out), .X_OUT(gpu_1_x_out), .Y_OUT(gpu_1_y_out));
  DipSwitch COLOR (
    .sw1(COLOR_sw8[7]), .sw2(COLOR_sw8[6]), .sw3(COLOR_sw8[5]), .sw4(COLOR_sw8[4]), .sw5(COLOR_sw8[3]),
    .sw6(COLOR_sw8[2]), .sw7(COLOR_sw8[1]), .sw8(COLOR_sw8[0]));
  LED led_23 (.in(cntr[19]));
  LED led_24 (.in(cntr[18]));
  LED led_25 (.in(cntr[17]));
  LED led_26 (.in(cntr[16]));
  LED led_27 (.in(pull_resistor_3_node[5]));
  LED led_28 (.in(pull_resistor_3_node[4]));
  LED led_29 (.in(pull_resistor_3_node[3]));
  LED led_30 (.in(pull_resistor_3_node[2]));
  LED led_31 (.in(cntr[15]));
  LED led_32 (.in(cntr[14]));
  LED led_33 (.in(cntr[13]));
  LED led_34 (.in(cntr[12]));
  LED led_35 (.in(pull_resistor_3_node[1]));
  LED led_36 (.in(pull_resistor_3_node[0]));
  Program_Counter program_counter_1 (
    .Reset(RESET), .JUMP(or_3_out), .Enable(TURN_ON), .Clock(cock),
    .DATA_IN({pull_resistor_3_node_2, pull_resistor_3_node}), .ALWAYS_OUT(cntr),
    .DATA_OUT({pull_resistor_3_node_2, pull_resistor_3_node}));  // open: READ
  ALU alu_1 (
    .A(XY), .B(multiplexer_2_out), .ADD(add), .SUB(sub), .MULT(mult), .DIV(div), .A_AND_B(and1),
    .A_OR_B(or1), .A_XOR_B(xor1), .NOT_A(not1), .LESS(alu_1_less), .CARRY(alu_1_carry),
    .BORROW(alu_1_borrow), .ZERO(alu_1_zero), .GREATER(alu_1_greater), .EQUAL(alu_1_equal),
    .RESULT({pull_resistor_3_node_2, pull_resistor_3_node}));
  Multiplexer #(.select(4), .width(24)) multiplexer_1 (
    .in0(gpr_1_l0), .in1(gpr_1_l1), .in2(gpr_1_l2), .in3(gpr_1_l3), .in4(gpr_1_l4), .in5(gpr_1_l5),
    .in6(gpr_1_l6), .in7(gpr_1_l7), .in8(gpr_1_l8), .in9(gpr_1_l9), .in10(gpr_1_l10), .in11(gpr_1_l11),
    .in12(gpr_1_l12), .in13(gpr_1_l13), .in14(gpr_1_l14), .in15(gpr_1_l15), .out(XY), .sel(A));
  Button MAN (.out(manual_t));
  Button u_RESET (.out(RESET));
  LED led_37 (.in(cntr[11]));
  LED led_38 (.in(cntr[10]));
  LED led_39 (.in(cntr[9]));
  LED led_40 (.in(cntr[8]));
  Pull_Resistor pull_resistor_4 (.node(cntr));
  FlagReg flagreg_1 (
    .GREATER(alu_1_greater), .EQUAL(alu_1_equal), .LESS(alu_1_less), .CARRY(alu_1_carry),
    .BORROW(alu_1_borrow), .ZERO(alu_1_zero), .COMP_FLAG(TURN_ON), .MATH_FLAGS(TURN_ON), .CLK(cock),
    .RST(RESET), .G_FLAG(G), .E_FLAG(E), .L_FLAG(L), .C_FLAG(CARRY), .B_FLAG(BORROW), .Z_FLAG(ZERO));
  GPR gpr_1 (
    .WRITE(gpr_w), .ADDR(multiplexer_3_out), .READ(gpr_r), .CLOCK(cock), .RESET(RESET),
    .DATA_IN({pull_resistor_3_node_2, pull_resistor_3_node}), .L7(gpr_1_l7), .L8(gpr_1_l8), .L9(gpr_1_l9),
    .L10(gpr_1_l10), .L11(gpr_1_l11), .L12(gpr_1_l12), .L13(gpr_1_l13), .L14(gpr_1_l14), .L15(gpr_1_l15),
    .L0(gpr_1_l0), .L1(gpr_1_l1), .L2(gpr_1_l2), .L3(gpr_1_l3), .L4(gpr_1_l4), .L5(gpr_1_l5), .L6(gpr_1_l6),
    .DATA_OUT({pull_resistor_3_node_2, pull_resistor_3_node}));
  RAM #(.addrWidth(12), .dataWidth(24), .\type ("nonvolatile")) ram_2 (
    .addr({D, C, B}), .we(ram_w), .oe(ram_r), .clk(cock),
    .din({pull_resistor_3_node_2, pull_resistor_3_node}), .dout(ram_2_dout));
  TTY tty_1 (.data(pull_resistor_3_node), .clk(cock), .we(text), .clr(RESET));
  Keyboard #(.buflen(256)) keyboard_1 (
    .clk(cock), .re(keybrd), .clr(CLEAR_out), .data(keyboard_1_data));  // open: avail
  Button CLEAR (.out(CLEAR_out));
  LED led_41 (.in(cntr[7]));
  LED led_42 (.in(cntr[6]));
  LED led_43 (.in(cntr[5]));
  LED led_44 (.in(cntr[4]));
  or or_3 (or_3_out, and_3_out, and_2_out, jump);
  LED led_45 (.in(cntr[3]));
  LED led_46 (.in(cntr[2]));
  LED led_47 (.in(cntr[1]));
  LED led_48 (.in(cntr[0]));
  and and_2 (and_2_out, JnotE, not_4_out);
  and and_3 (and_3_out, JE, E);
  Pull_Resistor pull_resistor_5 (.node(jump));
  Pull_Resistor pull_resistor_6 (.node(JnotE));
  not not_4 (not_4_out, E);
  Pull_Resistor pull_resistor_7 (.node(JE));
  Multiplexer #(.select(4), .width(24)) multiplexer_2 (
    .in0(gpr_1_l0), .in1(gpr_1_l1), .in2(gpr_1_l2), .in3(gpr_1_l3), .in4(gpr_1_l4), .in5(gpr_1_l5),
    .in6(gpr_1_l6), .in7(gpr_1_l7), .in8(gpr_1_l8), .in9(gpr_1_l9), .in10(gpr_1_l10), .in11(gpr_1_l11),
    .in12(gpr_1_l12), .in13(gpr_1_l13), .in14(gpr_1_l14), .in15(gpr_1_l15), .out(multiplexer_2_out), .sel(B));
  Multiplexer #(.select(2), .width(4)) multiplexer_3 (
    .in0(A), .in1(B), .in2(C), .in3(D), .out(multiplexer_3_out), .sel(cmd));
  assign {pull_resistor_3_node_2, pull_resistor_3_node} = ram_r ? ram_2_dout : 24'bz;  // Controlled_Buffer controlled_buffer_3
  // RGB_Video #(.height(64), .width(64)) rgb_video_1: pin names not known; wires that end beside it: RESET, cock, TurnOnMonitor, D, gpu_1_x_out, gpu_1_y_out, gpu_1_color_out
  assign controlled_buffer_4_out = keybrd ? keyboard_1_data : 7'bz;  // Controlled_Buffer controlled_buffer_4

  // Other names for the same wires on the sheet: clock_enable = EnableClock; ENABLE_t = TURN_ON

  // Notes on the sheet:
  //   contents of rom_1 (hex, n*v repeats v):
  //   0 12 40004 18 24 800044 800084 800104 800204 800404 800804 801004 402004 20004 10010 4000 8000 80000
  //   237*0 1
endmodule

module CLK (
  input  CLOCK,
  input  ENABLE,
  input  MANUAL,
  input  HALT,
  output CLOCKOUT
);

  wire and_1_out, and_2_out, not_1_out, not_2_out, or_1_out;

  and and_1 (and_1_out, CLOCK, ENABLE);
  not not_1 (not_1_out, ENABLE);
  and and_2 (and_2_out, not_1_out, MANUAL);
  or or_1 (or_1_out, and_1_out, and_2_out);
  not not_2 (not_2_out, HALT);
  and and_3 (CLOCKOUT, or_1_out, not_2_out);
endmodule

module Program_Counter (
  input  READ,
  input  Reset,
  input  JUMP,
  input  Enable,
  input  Clock,
  input  [23:0] DATA_IN,
  output [23:0] ALWAYS_OUT,
  output [23:0] DATA_OUT
);

  Counter #(.max('hffffff), .width(24)) counter_1 (
    .clr(Reset), .load(JUMP), .up(Enable), .count(Enable), .clk(Clock), .D(DATA_IN), .Q(ALWAYS_OUT));  // open: carry
  assign DATA_OUT = READ ? ALWAYS_OUT : 24'bz;  // Controlled_Buffer controlled_buffer_1
endmodule

module GPR (
  input  [23:0] DATA_IN,
  input  READ,
  input  WRITE,
  input  [3:0] ADDR,
  input  CLOCK,
  input  RESET,
  output [23:0] L0,
  output [23:0] L1,
  output [23:0] L2,
  output [23:0] L3,
  output [23:0] DATA_OUT,
  output [23:0] L4,
  output [23:0] L5,
  output [23:0] L6,
  output [23:0] L7,
  output [23:0] L8,
  output [23:0] L9,
  output [23:0] L10,
  output [23:0] L11,
  output [23:0] L12,
  output [23:0] L13,
  output [23:0] L14,
  output [23:0] L15
);

  wire decoder_1_out0, decoder_1_out1, decoder_1_out2, decoder_1_out3, decoder_1_out4, decoder_1_out5,
       decoder_1_out6, decoder_1_out7, decoder_1_out8, decoder_1_out9, decoder_1_out10, decoder_1_out11,
       decoder_1_out12, decoder_1_out13, decoder_1_out14, decoder_1_out15;
  wire [23:0] multiplexer_1_out;

  Decoder #(.select(4)) decoder_1 (
    .out0(decoder_1_out0), .out1(decoder_1_out1), .out2(decoder_1_out2), .out3(decoder_1_out3),
    .out4(decoder_1_out4), .out5(decoder_1_out5), .out6(decoder_1_out6), .out7(decoder_1_out7),
    .out8(decoder_1_out8), .out9(decoder_1_out9), .out10(decoder_1_out10), .out11(decoder_1_out11),
    .out12(decoder_1_out12), .out13(decoder_1_out13), .out14(decoder_1_out14), .out15(decoder_1_out15),
    .sel(ADDR), .en(WRITE));
  Register #(.width(24)) register_1 (.D(DATA_IN), .en(decoder_1_out0), .clk(CLOCK), .Q(L0), .clr(RESET));
  Register #(.width(24)) register_2 (.D(DATA_IN), .en(decoder_1_out1), .clk(CLOCK), .Q(L1), .clr(RESET));
  Register #(.width(24)) register_3 (.D(DATA_IN), .en(decoder_1_out2), .clk(CLOCK), .Q(L2), .clr(RESET));
  Register #(.width(24)) register_4 (.D(DATA_IN), .en(decoder_1_out3), .clk(CLOCK), .Q(L3), .clr(RESET));
  Register #(.width(24)) register_5 (.D(DATA_IN), .en(decoder_1_out4), .clk(CLOCK), .Q(L4), .clr(RESET));
  Register #(.width(24)) register_6 (.D(DATA_IN), .en(decoder_1_out5), .clk(CLOCK), .Q(L5), .clr(RESET));
  Register #(.width(24)) register_7 (.D(DATA_IN), .en(decoder_1_out6), .clk(CLOCK), .Q(L6), .clr(RESET));
  Register #(.width(24)) register_8 (.D(DATA_IN), .en(decoder_1_out7), .clk(CLOCK), .Q(L7), .clr(RESET));
  Register #(.width(24)) register_9 (.D(DATA_IN), .en(decoder_1_out8), .clk(CLOCK), .Q(L8), .clr(RESET));
  Register #(.width(24)) register_10 (.D(DATA_IN), .en(decoder_1_out9), .clk(CLOCK), .Q(L9), .clr(RESET));
  Register #(.width(24)) register_11 (.D(DATA_IN), .en(decoder_1_out10), .clk(CLOCK), .Q(L10), .clr(RESET));
  Register #(.width(24)) register_12 (.D(DATA_IN), .en(decoder_1_out11), .clk(CLOCK), .Q(L11), .clr(RESET));
  Register #(.width(24)) register_13 (.D(DATA_IN), .en(decoder_1_out12), .clk(CLOCK), .Q(L12), .clr(RESET));
  Register #(.width(24)) register_14 (.D(DATA_IN), .en(decoder_1_out13), .clk(CLOCK), .Q(L13), .clr(RESET));
  Register #(.width(24)) register_15 (.D(DATA_IN), .en(decoder_1_out14), .clk(CLOCK), .Q(L14), .clr(RESET));
  Register #(.width(24)) register_16 (.D(DATA_IN), .en(decoder_1_out15), .clk(CLOCK), .Q(L15), .clr(RESET));
  Multiplexer #(.select(4), .width(24)) multiplexer_1 (
    .in0(L0), .in1(L1), .in2(L2), .in3(L3), .in4(L4), .in5(L5), .in6(L6), .in7(L7), .in8(L8), .in9(L9),
    .in10(L10), .in11(L11), .in12(L12), .in13(L13), .in14(L14), .in15(L15), .out(multiplexer_1_out),
    .sel(ADDR));
  assign DATA_OUT = READ ? multiplexer_1_out : 24'bz;  // Controlled_Buffer controlled_buffer_1

  // Other names for the same wires on the sheet: AD[3:0] = ADDR
endmodule

module ALU (
  input  [23:0] A,
  input  [23:0] B,
  input  ADD,
  input  SUB,
  input  MULT,
  input  DIV,
  input  A_AND_B,
  input  A_OR_B,
  input  A_XOR_B,
  input  NOT_A,
  output GREATER,
  output EQUAL,
  output LESS,
  output CARRY,
  output BORROW,
  output ZERO,
  output [23:0] RESULT
);

  wire [23:0] adder_1_out, and_1_out, divider_1_out, multiplier_1_out, not_1_out, or_1_out, subtractor_1_out,
       xor_1_out;

  Comparator #(.width(24)) comparator_1 (.a(A), .b(B), .gt(GREATER), .eq(EQUAL), .lt(LESS));
  assign RESULT = ADD ? adder_1_out : 24'bz;  // Controlled_Buffer controlled_buffer_1
  Adder #(.width(24)) adder_1 (.a(A), .b(B), .out(adder_1_out), .cout(CARRY));  // open: cin
  assign RESULT = SUB ? subtractor_1_out : 24'bz;  // Controlled_Buffer controlled_buffer_2
  Subtractor #(.width(24)) subtractor_1 (.a(A), .b(B), .out(subtractor_1_out), .bout(BORROW));  // open: bin
  assign RESULT = MULT ? multiplier_1_out : 24'bz;  // Controlled_Buffer controlled_buffer_3
  Multiplier #(.width(24)) multiplier_1 (.a(A), .b(B), .out(multiplier_1_out));  // open: cin, cout
  assign RESULT = DIV ? divider_1_out : 24'bz;  // Controlled_Buffer controlled_buffer_4
  Divider #(.width(24)) divider_1 (.a(A), .b(B), .out(divider_1_out));  // open: upper, rem
  assign and_1_out = A & B;  // AND_Gate and_1, 24 bits wide
  assign RESULT = A_AND_B ? and_1_out : 24'bz;  // Controlled_Buffer controlled_buffer_5
  assign or_1_out = A | B;  // OR_Gate or_1, 24 bits wide
  assign RESULT = A_OR_B ? or_1_out : 24'bz;  // Controlled_Buffer controlled_buffer_6
  assign xor_1_out = A ^ B;  // XOR_Gate xor_1, 24 bits wide
  assign not_1_out = ~A;  // NOT_Gate not_1, 24 bits wide
  assign RESULT = NOT_A ? not_1_out : 24'bz;  // Controlled_Buffer controlled_buffer_7
  assign RESULT = A_XOR_B ? xor_1_out : 24'bz;  // Controlled_Buffer controlled_buffer_8
  Comparator #(.width(24)) comparator_2 (.a({24{1'b0}}), .b(RESULT), .eq(ZERO));  // open: gt, lt
endmodule

module FlagReg (
  input  GREATER,
  input  EQUAL,
  input  LESS,
  input  CARRY,
  input  BORROW,
  input  ZERO,
  input  COMP_FLAG,
  input  MATH_FLAGS,
  input  CLK,
  input  RST,
  output G_FLAG,
  output E_FLAG,
  output L_FLAG,
  output C_FLAG,
  output B_FLAG,
  output Z_FLAG
);

  Register #(.width(1)) register_1 (.D(GREATER), .en(COMP_FLAG), .clk(CLK), .Q(G_FLAG), .clr(RST));
  Register #(.width(1)) register_2 (.D(EQUAL), .en(COMP_FLAG), .clk(CLK), .Q(E_FLAG), .clr(RST));
  Register #(.width(1)) register_3 (.D(LESS), .en(COMP_FLAG), .clk(CLK), .Q(L_FLAG), .clr(RST));
  Register #(.width(1)) register_4 (.D(CARRY), .en(MATH_FLAGS), .clk(CLK), .Q(C_FLAG), .clr(RST));
  Register #(.width(1)) register_5 (.D(BORROW), .en(MATH_FLAGS), .clk(CLK), .Q(B_FLAG), .clr(RST));
  Register #(.width(1)) register_6 (.D(ZERO), .en(MATH_FLAGS), .clk(CLK), .Q(Z_FLAG), .clr(RST));
endmodule

module GPU (
  input  RESET,
  input  DRAW,
  input  CLOCK,
  input  [7:0] COLOR,
  input  ENABLE,
  input  WRITE,
  input  [11:0] XY,
  output [7:0] COLOR_OUT,
  output [5:0] X_OUT,
  output [5:0] Y_OUT
);

  wire and_1_out, X_cnt_carry;
  wire [7:0] ram_1_dout;

  and and_1 (and_1_out, ENABLE, X_cnt_carry);
  RAM #(.addrWidth(12)) ram_1 (
    .addr({Y_OUT, X_OUT}), .we(DRAW), .oe(ENABLE), .clk(CLOCK), .din(COLOR), .dout(ram_1_dout));
  Counter #(.max('h3f), .width(6)) X_cnt (
    .clr(RESET), .load(WRITE), .up(ENABLE), .count(ENABLE), .clk(CLOCK), .D(XY[5:0]), .carry(X_cnt_carry),
    .Q(X_OUT));
  Counter #(.max('h3f), .width(6)) Y_cnt (
    .clr(RESET), .load(WRITE), .up(and_1_out), .count(and_1_out), .clk(CLOCK), .D(XY[11:6]), .Q(Y_OUT));  // open: carry
  Pull_Resistor pull_resistor_1 (.node(COLOR_OUT));
  assign COLOR_OUT = DRAW ? ram_1_dout : 8'bz;  // Controlled_Buffer controlled_buffer_1
endmodule
